# Fritzing sketch circuito (saved by Fritzing 0.4.3b)
breadboards: 1

parts:
  Arduino1 = Arduino
  R1 = Photocell (LDR) [package=THT]
  R2 = Photocell (LDR) [package=THT]
  LED1 = Red LED - 5mm
  R3 = Resistor [resistance=220 package=THT]
  R4 = Resistor [resistance=220 package=THT]
  LED2 = green LED - 5mm
  LED3 = Blue LED - 5mm
  R5 = Resistor [resistance=1k package=THT]
  R5_2 = Resistor [resistance=1k package=THT]
  R5_3 = Resistor [resistance=1k package=THT]
  J1 = Basic Servo

nets:
  N1: Arduino1.D9, J1.pulse
  N2: Arduino1.D2, LED3.anode
  N3: Arduino1.D1TX, LED2.anode
  N4: Arduino1.D0RX, LED1.anode
  +5V: Arduino1.+5V, R1.pin_1, R2.pin_1, J1.vcc
  GND: Arduino1.GND, R3.Pin_0, R4.Pin_0, R5.Pin_1, R5_2.Pin_1, R5_3.Pin_1, J1.gnd
  N5: Arduino1.A0, R1.pin_0, R3.Pin_1
  N6: Arduino1.A1, R2.pin_0, R4.Pin_1
  N7: LED1.cathode, R5.Pin_0
  N8: LED2.cathode, R5_2.Pin_0
  N9: LED3.cathode, R5_3.Pin_0
